# Fritzing sketch brainedit (saved by Fritzing 0.9.2b)
circuit board: 8.46667cm x 5.64444cm
breadboards: 1

parts:
  Bauteil1 = Arduino Micro (Rev3)
  Right_Eye = LED - 5mm [color="Red (633nm)" package="5 mm [THT]"]
  Left_Eye = LED - 5mm [color="Red (633nm)" package="5 mm [THT]"]

nets:
  N1: Bauteil1.GND, Right_Eye.anode, Left_Eye.anode
  N2: Bauteil1.D7, Right_Eye.cathode
  N3: Bauteil1.D10_PWM/A10, Left_Eye.cathode

// code stored in the sketch: arduino.ino
#define rightEyeRed 7 // Define pinout for right eye
#define leftEyeRed 10 // Define pinout for left eye
#define led 13 // Define pinout for status

int waittime = 100;
int alt = 3;

void setup() {                
  pinMode(rightEyeRed, OUTPUT); // Pin output at rightEyeRed
  pinMode(leftEyeRed, OUTPUT); // Pin output at leftEyeRed 
  Serial.begin(115200);  
}

// the loop routine runs over and over again forever:
void loop() {
  if (Serial.available() > 0) {
    waittime = Serial.parseInt();
    alt = Serial.parseInt();
    if (Serial.read() == '\n') {
      Serial.println(waittime);
      Serial.println(alt);

    }
  }
  if(waittime==0){
    analogWrite(rightEyeRed, 0); 
    analogWrite(leftEyeRed, 0);
    analogWrite(led, 0);
    delay(100); 
  } else if(alt==0){ // normal blink
    analogWrite(rightEyeRed, 0); 
    analogWrite(leftEyeRed, 0); 
    analogWrite(led, 0);
    delay(waittime); 
  
    analogWrite(rightEyeRed, 255);
    analogWrite(leftEyeRed, 255);
    analogWrite(led, 255);
    delay(waittime); 
  } else if(alt==1) { //alt blink
    analogWrite(rightEyeRed, 0); 
    analogWrite(leftEyeRed, 255);
    analogWrite(led, 0);   
    delay(waittime);     
  
    analogWrite(rightEyeRed, 255); 
    analogWrite(leftEyeRed, 0); 
    analogWrite(led, 255);
    delay(waittime); 
  } else {
    analogWrite(rightEyeRed, 255); 
    analogWrite(leftEyeRed, 255);
    analogWrite(led, 255); 
  }
   
}

// code stored in the sketch: Untitled.ino
#define rightEyeRed 7 // Define pinout for right eye
#define leftEyeRed 10 // Define pinout for left eye
#define led 13 // Define pinout for status

int waittime = 100;
int alt = 3;

void setup() {                
  pinMode(rightEyeRed, OUTPUT); // Pin output at rightEyeRed
  pinMode(leftEyeRed, OUTPUT); // Pin output at leftEyeRed 
  Serial.begin(115200);  
}

// the loop routine runs over and over again forever:
void loop() {
  if (Serial.available() > 0) {
    waittime = Serial.parseInt();
    alt = Serial.parseInt();
    if (Serial.read() == '\n') {
      Serial.println(waittime);
      Serial.println(alt);

    }
  }
  if(waittime==0){
    analogWrite(rightEyeRed, 0); 
    analogWrite(leftEyeRed, 0);
    analogWrite(led, 0);
    delay(100); 
  } else if(alt==0){ // normal blink
    analogWrite(rightEyeRed, 0); 
    analogWrite(leftEyeRed, 0); 
    analogWrite(led, 0);
    delay(waittime); 
  
    analogWrite(rightEyeRed, 255);
    analogWrite(leftEyeRed, 255);
    analogWrite(led, 255);
    delay(waittime); 
  } else if(alt==1) { //alt blink
    analogWrite(rightEyeRed, 0); 
    analogWrite(leftEyeRed, 255);
    analogWrite(led, 0);   
    delay(waittime);     
  
    analogWrite(rightEyeRed, 255); 
    analogWrite(leftEyeRed, 0); 
    analogWrite(led, 255);
    delay(waittime); 
  } else {
    analogWrite(rightEyeRed, 255); 
    analogWrite(leftEyeRed, 255);
    analogWrite(led, 255); 
  }
   
}
